# Fritzing sketch Auto_shelf_elc_draw (saved by Fritzing 0.9.3b)

parts:
  Part1 = Arduino Uno (Rev3)
  L298N1 = L298N DC motor driver
  Mod1 = KY-022 Infrared Receiver Module [package="Breakout board"]
  M2 = Stepper Motor - Bipolar
  R1 = Resistor [tolerance=±5% resistance=10k package="0603 [SMD]"]
  R2 = Resistor [tolerance=±5% resistance=10k package="0603 [SMD]"]
  V1 = DC Power [voltage=12V frequency=60]  # not connected
  S1 = Round Pushbutton
  JACK1 = 2.1mm Barrel Jack with Terminal Block
  M3 = LJ12A3-4-Z [package=THT]  # not connected
  M4 = LJ12A3-4-Z [package=THT]  # not connected

nets:
  N1: Part1.D8, S1.leg0
  N2: Part1.D11_PWM/MOSI, Mod1.S
  GND: Part1.GND, L298N1.GND, Mod1.-, S1.leg1, JACK1.NEG
  N3: Part1.D2, R2.Pin_0
  N4: Part1.D3_PWM, R1.Pin_0
  N5: Part1.D4, L298N1.ENA, L298N1.IN1
  N6: Part1.D5_PWM, L298N1.IN2
  N7: Part1.D6_PWM, L298N1.IN3
  N8: Part1.D7, L298N1.ENB, L298N1.IN4
  5V: Part1.5V, Mod1.Vin
  N9: L298N1.OUT1, M2.A
  N10: L298N1.OUT2, M2.C
  N11: L298N1.OUT3, M2.B
  N12: L298N1.OUT4, M2.D
  N13: L298N1.12V, JACK1.POS

custom parts:
  L298N DC motor driver: 2x DC motor driver with 78M05 positive voltage regulator (7..35 V) L298N: max 46 V, 2 A Set 5 V Enable jumper to enable 5 V regultor (needed for the L298N) and +5 V output at screw terminal or supply external +5 V at screw terminal Set ENA and/or ENB to +5 V to enable motor permanently or supply ENA and/or ENB with PWM signal IN1 and IN2 set rotation directory for motor A (OUT1/OUT2) IN2 and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
  KY-022 Infrared Receiver Module: KY-022 IR receiver module, reacts to 38kHz infrared light.
  LJ12A3-4-Z: LJ12A3-4-Z Proximity Sensor module.220V normally open.
